# Fritzing sketch Ac-vent-filter (saved by Fritzing 0.9.3b)
breadboards: 1

parts:
  RHT1 = Humidity and Temperature Sensor RHT03
  S1 = Pushbutton [package="[THT]"]
  S2 = Pushbutton [package="[THT]"]
  S3 = Pushbutton [package="[THT]"]
  J1 = Basic Servo
  Part2 = Arduino Uno (Rev3)
  R1 = Resistor [tolerance=±5% resistance=220 package="2512 [SMD]"]
  R2 = Resistor [tolerance=±5% resistance=220 package="2512 [SMD]"]
  R3 = Resistor [tolerance=±5% resistance=220 package="2512 [SMD]"]
  U2 = LCD-16X2 [package=lcd-16x2]  # not connected
  Part3 = Ludus ProtoShield Wireless  # not connected

nets:
  VCC: RHT1.Vcc, S1.Pin_1, S1.Pin_2, S2.Pin_1, S2.Pin_2, S3.Pin_1, S3.Pin_2, J1.vcc, Part2.5V
  N1: RHT1.Data-signal, Part2.D1/TX
  GND: RHT1.GND_2, J1.gnd, Part2.GND, R1.Pin_1, R2.Pin_1, R3.Pin_1
  N2: S1.Pin_3, S1.Pin_4, Part2.D13/SCK, R1.Pin_0
  N3: S2.Pin_3, S2.Pin_4, Part2.D12/MISO, R2.Pin_0
  N4: S3.Pin_3, S3.Pin_4, Part2.D7, R3.Pin_0
  N5: J1.pulse, Part2.D0/RX

// code stored in the sketch: ac-cover.ino

