# Fritzing sketch moisture sensor (saved by Fritzing 0.9.3b)
breadboards: 1

parts:
  S1 = Pushbutton [package="[THT]"]
  S2 = Pushbutton [package="[THT]"]
  Part1 = Soil Moisture Sensor
  R2 = Resistor [tolerance=±5% resistance=1 package=THT]
  LED1 = LED - 5mm [color="Green (560nm)" package="5 mm [THT]"]
  LED2 = LED - 5mm [color="Yellow (592nm)" package="5 mm [THT]"]
  Part2 = Arduino Uno (Rev3)
  R3 = Resistor [tolerance=±5% resistance=220 package=THT]
  R4 = Resistor [tolerance=±5% resistance=220 package=THT]
  R5 = Resistor [tolerance=±5% resistance=1 package=THT]
  LED3 = LED - 5mm [color="Red (633nm)" package="5 mm [THT]"]
  R6 = Resistor [tolerance=±5% resistance=220 package=THT]

nets:
  N1: S1.Pin_1, S1.Pin_2, Part2.D0/RX, R5.Pin_1
  N2: S1.Pin_3, S1.Pin_4, S2.Pin_3, S2.Pin_4, Part2.5V
  N3: S2.Pin_1, S2.Pin_2, R2.Pin_1, Part2.D1/TX
  N4: Part1.SIG, Part2.D7
  GND: Part1.GND, R2.Pin_0, Part2.GND, R3.Pin_0, R4.Pin_0, R5.Pin_0, R6.Pin_0
  N5: Part1.VCC, Part2.A0
  N6: LED1.cathode, R4.Pin_1
  N7: LED1.anode, Part2.D9_PWM
  N8: LED2.cathode, R3.Pin_1
  N9: LED2.anode, Part2.D8
  N10: Part2.D10_PWM/SS, LED3.anode
  N11: LED3.cathode, R6.Pin_1
